# Fritzing sketch Fly-farmer (saved by Fritzing 0.9.3b)
breadboards: 2

parts:
  Part1 = Arduino Mega 2560 (Rev3)
  Pololu_A2 = Pololu A4988 [package=SO16]
  Pololu_A5 = Pololu A4988 [package=SO16]
  C1 = Capacitor Polarized [package=cpol-radial-10uf-25v]
  M1 = Stepper Motor - Bipolar
  C2 = Capacitor Polarized [package=cpol-radial-10uf-25v]
  M2 = Stepper Motor - Bipolar
  Pololu_A6 = Pololu A4988 [package=SO16]
  C3 = Capacitor Polarized [package=cpol-radial-10uf-25v]
  M3 = Stepper Motor - Bipolar
  Pololu_A7 = Pololu A4988 [package=SO16]
  M4 = Stepper Motor - Bipolar
  C4 = Capacitor Polarized [package=cpol-radial-10uf-25v]
  Pololu_A8 = Pololu A4988 [package=SO16]
  C5 = Capacitor Polarized [package=cpol-radial-10uf-25v]
  Power_plug1 = Power plug
  M5 = Stepper Motor - Bipolar
  D2F1 = D2F-FL Omron Snap Action Limit Switch with Level
  D2F2 = D2F-FL Omron Snap Action Limit Switch with Level
  D2F3 = D2F-FL Omron Snap Action Limit Switch with Level
  D2F4 = D2F-FL Omron Snap Action Limit Switch with Level
  D2F5 = D2F-FL Omron Snap Action Limit Switch with Level
  D2F6 = D2F-FL Omron Snap Action Limit Switch with Level
  D2F7 = D2F-FL Omron Snap Action Limit Switch with Level
  D2F8 = D2F-FL Omron Snap Action Limit Switch with Level
  R1 = Resistor [tolerance=±5% resistance=10k package=THT]
  R2 = Resistor [tolerance=±5% resistance=10k package=THT]
  R3 = Resistor [tolerance=±5% resistance=10k package=THT]
  R4 = Resistor [tolerance=±5% resistance=10k package=THT]
  R5 = Resistor [tolerance=±5% resistance=10k package=THT]
  R6 = Resistor [tolerance=±5% resistance=10k package=THT]
  R7 = Resistor [tolerance=±5% resistance=10k package=THT]
  R9 = Resistor [tolerance=±5% resistance=10k package=THT]

nets:
  N1: Part1.D11_PWM, Pololu_A8.STEP
  N2: Part1.D10_PWM, Pololu_A8.DIR
  N3: Part1.D9_PWM, Pololu_A7.STEP
  N4: Part1.D8_PWM, Pololu_A7.DIR
  VDD: Part1.5V, Pololu_A2.VDD, Pololu_A5.VDD, Pololu_A6.VDD, Pololu_A7.VDD, Pololu_A8.VDD, D2F1.COM, D2F4.COM, D2F6.COM, D2F7.COM, D2F8.COM
  N5: Part1.GND, Pololu_A2.GND#8, Pololu_A5.GND#8, Pololu_A6.GND#8, Pololu_A7.GND#8, Pololu_A8.GND#8, R5.Pin_0, R6.Pin_0, R9.Pin_0
  N6: Part1.D2_PWM, Pololu_A6.DIR
  N7: Part1.D3_PWM, Pololu_A6.STEP
  N8: Part1.D4_PWM, Pololu_A2.STEP
  N9: Part1.D5_PWM, Pololu_A2.DIR
  N10: Part1.D6_PWM, Pololu_A5.DIR
  N11: Part1.D7_PWM, Pololu_A5.STEP
  N12: Part1.D22, D2F8.NO, R9.Pin_1
  N13: Part1.D24, D2F7.NO, R7.Pin_1
  N14: Part1.D26, D2F6.NO, R5.Pin_1
  N15: Part1.D28, D2F4.NO, R6.Pin_1
  N16: Part1.D30, D2F1.NO, R1.Pin_1
  N17: Part1.D32, D2F2.NO, R2.Pin_1
  N18: Part1.D34, D2F3.NO, R4.Pin_1
  N19: Part1.D36, D2F5.NO, R3.Pin_1
  N20: Pololu_A2.RESET, Pololu_A2.SLEEP
  N21: Pololu_A2.1B, M1.D
  N22: Pololu_A2.1A, M1.B
  N23: Pololu_A2.2A, M1.C
  N24: Pololu_A2.2B, M1.A
  N25: Pololu_A2.GND#14, C1.-, Pololu_A6.GND#14, C3.-, Pololu_A7.GND#14, C4.-, Pololu_A8.GND#14, C5.-, Power_plug1.GND
  N26: Pololu_A2.VMOT, C1.+, Pololu_A6.VMOT, C3.+, Pololu_A7.VMOT, C4.+, Pololu_A8.VMOT, C5.+, Power_plug1.VCC
  N27: Pololu_A5.1B, M2.D
  N28: Pololu_A5.1A, M2.B
  N29: Pololu_A5.2A, M2.C
  N30: Pololu_A5.2B, M2.A
  N31: Pololu_A5.GND#14, C2.-
  N32: Pololu_A5.VMOT, C2.+
  N33: Pololu_A6.RESET, Pololu_A6.SLEEP
  N34: Pololu_A6.1B, M3.D
  N35: Pololu_A6.1A, M3.B
  N36: Pololu_A6.2A, M3.C
  N37: Pololu_A6.2B, M3.A
  N38: Pololu_A7.RESET, Pololu_A7.SLEEP
  N39: Pololu_A7.1B, M4.D
  N40: Pololu_A7.1A, M4.B
  N41: Pololu_A7.2A, M4.C
  N42: Pololu_A7.2B, M4.A
  N43: Pololu_A8.RESET, Pololu_A8.SLEEP
  N44: Pololu_A8.1B, M5.D
  N45: Pololu_A8.1A, M5.B
  N46: Pololu_A8.2A, M5.C
  N47: Pololu_A8.2B, M5.A
  N48: D2F2.COM, D2F3.COM, D2F5.COM
  N49: R1.Pin_0, R2.Pin_0, R3.Pin_0, R4.Pin_0

notes:
  12v power supply
  Cleaning Door Stepper
  Pupae door stepper
  Egg tray door 1 stepper
  Egg tray door 2 stepper
  Egg tray door 3 stepper
  cleaning door forward limit switch
  cleaning door backward limit switch
  pupae door forward limit switch
  pupae door backward limit switch
  etd1 door backward limit switch
  etd1 door forward limit switch
  etd2 door forward limit switch
  etd2 door backward limit switch

custom parts:
  D2F-FL Omron Snap Action Limit Switch with Level: Snap action switch with stainless steel lever.
